# Fritzing sketch 2015Schematic (saved by Fritzing 0.9.2b)
breadboards: 1

parts:
  MC33926_Motor_Driver = Header 6 [package=1x06-smd]
  MC33926_Motor_Driver1 = Header 6 [package=1x06-smd]
  MC33926_Motor_Driver2 = Header 6 [package=1x06-smd]
  MC33926_Motor_Driver4 = Header 6 [package=1x06-smd]
  MC33926_Motor_Driver5 = Header 6 [package=1x06-smd]
  Power_In = Header 2 [package=springterminal-2.54mm-2]
  20_Amp_Fuse = FUSE [package=fuse_5mm]
  MC33926_Motor_Driver3 = Header 6 [package=1x06-smd]
  M1 = DC Motor
  M2 = DC Motor
  M3 = DC Motor
  M4 = DC Motor
  M5 = DC Motor
  M6 = DC Motor
  Part1 = Arduino Mega 2560 (Rev3)
  J1 = Basic Servo
  J2 = Basic Servo
  J3 = Basic Servo
  12v_to_5v = Header 2 [package=springterminal-2.54mm-2]
  JP4 = Header 2 [package=springterminal-2.54mm-2]

nets:
  N1: MC33926_Motor_Driver.1, MC33926_Motor_Driver1.1, MC33926_Motor_Driver2.1, MC33926_Motor_Driver4.1, MC33926_Motor_Driver5.1, 20_Amp_Fuse.1, MC33926_Motor_Driver3.1, JP4.1
  N2: MC33926_Motor_Driver.2, MC33926_Motor_Driver1.2, MC33926_Motor_Driver2.2, MC33926_Motor_Driver4.2, MC33926_Motor_Driver5.2, Power_In.2, MC33926_Motor_Driver3.2, JP4.2
  N3: MC33926_Motor_Driver.3, M6.pin_2
  N4: MC33926_Motor_Driver.4, M6.pin_1
  N5: MC33926_Motor_Driver.5, Part1.D5_PWM
  N6: MC33926_Motor_Driver.6, Part1.D34
  N7: MC33926_Motor_Driver1.3, M5.pin_2
  N8: MC33926_Motor_Driver1.4, M5.pin_1
  N9: MC33926_Motor_Driver1.5, Part1.D6_PWM
  N10: MC33926_Motor_Driver1.6, Part1.D33
  N11: MC33926_Motor_Driver2.3, M4.pin_2
  N12: MC33926_Motor_Driver2.4, M4.pin_1
  N13: MC33926_Motor_Driver2.5, Part1.D7_PWM
  N14: MC33926_Motor_Driver2.6, Part1.D32
  N15: MC33926_Motor_Driver4.3, M2.pin_2
  N16: MC33926_Motor_Driver4.4, M2.pin_1
  N17: MC33926_Motor_Driver4.5, Part1.D3_PWM
  N18: MC33926_Motor_Driver4.6, Part1.D36
  N19: MC33926_Motor_Driver5.3, M3.pin_2
  N20: MC33926_Motor_Driver5.4, M3.pin_1
  N21: MC33926_Motor_Driver5.5, Part1.D4_PWM
  N22: MC33926_Motor_Driver5.6, Part1.D37
  N23: Power_In.1, 20_Amp_Fuse.2
  N24: MC33926_Motor_Driver3.3, M1.pin_2
  N25: MC33926_Motor_Driver3.4, M1.pin_1
  N26: MC33926_Motor_Driver3.5, Part1.D2_PWM
  N27: MC33926_Motor_Driver3.6, Part1.D35
  N28: Part1.D13_PWM, J3.pulse
  N29: Part1.D12_PWM, J2.pulse
  N30: Part1.D11_PWM, J1.pulse
  GND: J1.gnd, J2.gnd, J3.gnd, 12v_to_5v.1
  VCC: J1.vcc, J2.vcc, J3.vcc, 12v_to_5v.2

notes:
  Maret MATE ROV Electrical Diagram, 1.2.1
  red=positive, black=ground, pink=servoData, yellow=motorSpeed, green=motorDirection, orange=motorPositive, cyan=motorNegative
